# Fritzing sketch ModeloLogico (saved by Fritzing 0.9.5d)
breadboards: 1

parts:
  Componente1 = Arduino Due (Rev2b)
  VCC1 = Battery block 9V
  Componente2 = MQ-4
  ESP32_-_Back1 = ESP32 - CAM
  Mod1 = gy-906
  J1 = Piezo Speaker

nets:
  N1: Componente1.A0, Componente2.AO
  N2: Componente1.D18/TX1, ESP32_-_Back1.GPIO1_/_TX
  N3: Componente1.D19/RX1, ESP32_-_Back1.GPIO3_/_RX
  N4: Componente1.IOREF, Mod1.VIN
  5V: Componente1.5V, VCC1.+, Componente2.VCC, ESP32_-_Back1.5V
  GND: Componente1.GND, VCC1.-, Componente2.GND, ESP32_-_Back1.GND, Mod1.GND, J1.pin1
  N5: Componente1.D3_PWM, J1.pin2
  N6: Componente1.D22, Mod1.SCL
  N7: Componente1.D23, Mod1.SDA

custom parts:
  Battery block 9V: 9 Volt battery block with 200mil pcb footprint spacing
  ESP32 - CAM: The ESP32-CAM has a very competitive small-size camera module that can operate independently as a minimum system with a footprint of only 27*40.5*4.5mm and a deep sleep current of up to 6mA.
  gy-906: gy-906 Non-contact PIR I2C interface temperature sensor breakout board.
